// Logisim project logisim_lab.circ as structural Verilog: 4 circuits, main circuit main
module main (
);

  ALUControlCircuit alucontrolcircuit_1 ();  // open: I30, I14, I13, I12, I5, I4, ALU_Ctrl3, ALU_Ctrl2, ALU_Ctrl1, ALU_Ctrl0, ALU_Src
  ImmGen immgen_1 ();  // open: Instruction, Imm32
  DRAM16Mx32byte dram16mx32byte_1 ();  // open: Address, WriteEnable, OutputEnable, DataIn, DataOut
endmodule

module ALUControlCircuit (
  input  I30,
  input  I14,
  input  I13,
  input  I12,
  input  I5,
  input  I4,
  output ALU_Ctrl3,
  output ALU_Ctrl2,
  output ALU_Ctrl1,
  output ALU_Ctrl0,
  output ALU_Src
);

  wire and_2_out, not_1_out, not_2_out, not_3_out, not_4_out, not_5_out;

  not not_1 (not_1_out, I14);
  not not_2 (not_2_out, I13);
  not not_3 (not_3_out, I12);
  not not_4 (not_4_out, I5);
  not not_5 (not_5_out, I4);
  and and_1 (ALU_Ctrl2, I30, not_2_out, I5);
  or or_1 (ALU_Ctrl1, not_2_out, not_5_out);
  or or_2 (ALU_Ctrl0, not_1_out, and_2_out);
  and and_2 (and_2_out, I13, not_3_out);
  or or_3 (ALU_Src, not_4_out, not_5_out);

  assign ALU_Ctrl3 = 1'b0;
endmodule

module ImmGen (
  input  [31:0] Instruction,
  output [31:0] Imm32
);

  Multiplexer #(.width(4)) multiplexer_1 (
    .in0(Instruction[24:21]), .in1(Instruction[11:8]), .out(Imm32[4:1]), .sel(Instruction[5]));
  Multiplexer multiplexer_2 (.in0(Instruction[31]), .in1(Instruction[7]), .out(Imm32[11]), .sel(Instruction[6]));
  Multiplexer #(.select(2)) multiplexer_3 (
    .in0(Instruction[20]), .in1(Instruction[7]), .in3(1'b0), .out(Imm32[0]), .sel(Instruction[6:5]));  // open: in2
  assign Imm32[31:12] = {{19{Instruction[31]}}, Instruction[31]};  // Bit_Extender bit_extender_1

  assign Imm32[10:5] = Instruction[30:25];

  // Other names for the same wires on the sheet: I30_25[5:0] = Instruction[30:25]; I5 = Instruction[5];
  //   I6_5[1:0] = Instruction[6:5]; I6 = Instruction[6]; I7 = Instruction[7]; I11_8[3:0] = Instruction[11:8];
  //   I20 = Instruction[20]; I24_21[3:0] = Instruction[24:21]; I31 = Instruction[31]
endmodule

module DRAM16Mx32byte (
  input  [25:0] Address,
  input  WriteEnable,
  input  OutputEnable,
  input  [31:0] DataIn,
  output [31:0] DataOut
);

  wire clock_1_out;

  Clock clock_1 (.out(clock_1_out));
  RAM #(.addrWidth(24)) ram_1 (
    .addr(Address[25:2]), .we(WriteEnable), .oe(OutputEnable), .clk(clock_1_out), .din(DataIn[31:24]),
    .dout(DataOut[31:24]));
  RAM #(.addrWidth(24)) ram_2 (
    .addr(Address[25:2]), .we(WriteEnable), .oe(OutputEnable), .clk(clock_1_out), .din(DataIn[23:16]),
    .dout(DataOut[23:16]));
  RAM #(.addrWidth(24)) ram_3 (
    .addr(Address[25:2]), .we(WriteEnable), .oe(OutputEnable), .clk(clock_1_out), .din(DataIn[15:8]),
    .dout(DataOut[15:8]));
  RAM #(.addrWidth(24)) ram_4 (
    .addr(Address[25:2]), .we(WriteEnable), .oe(OutputEnable), .clk(clock_1_out), .din(DataIn[7:0]),
    .dout(DataOut[7:0]));
endmodule
